# Fritzing sketch MIDIsonar Fritzing Design (saved by Fritzing 0.9.3b)
breadboards: 2

parts:
  Onderdeel1 = Arduino Uno (Rev3)
  LCD_screen = LCD screen
  MODE = Pushbutton [package="[THT]"]
  PREV = Pushbutton [package="[THT]"]
  R4 = Trimmer Potentiometer [maximum_resistance=10kΩ package=THT]
  R3 = Resistor [tolerance=±5% resistance=220 package=THT]
  Sonar_B = SRF05 Ultrasonic Rangefinder
  Sonar_A = SRF05 Ultrasonic Rangefinder
  MIDI_Out = DIN-5 jack (MIDI) [package=THT]
  R5 = Resistor [tolerance=±5% resistance=10k package=THT]
  R6 = Resistor [tolerance=±5% resistance=10k package=THT]
  R7 = Resistor [tolerance=±5% resistance=10k package=THT]
  R8 = Resistor [tolerance=±5% resistance=220 package=THT]
  R9 = Resistor [tolerance=±5% resistance=220 package=THT]
  Led_A = LED - 5mm [color="Blue (470nm)" package="5 mm [THT]"]
  Led_B = LED - 5mm [color="Blue (470nm)" package="5 mm [THT]"]
  R10 = Resistor [tolerance=±5% resistance=220 package=THT]
  R11 = Resistor [tolerance=±5% resistance=220 package=THT]
  NEXT = Pushbutton [package="[THT]"]
  INC = Pushbutton [package="[THT]"]
  DEC = Pushbutton [package="[THT]"]
  R12 = Resistor [tolerance=±5% resistance=10k package=THT]
  R13 = Resistor [tolerance=±5% resistance=10k package=THT]

nets:
  N1: Onderdeel1.A1, MODE.Pin_3, MODE.Pin_4, R5.Pin_0
  N2: Onderdeel1.A2, PREV.Pin_3, PREV.Pin_4, R6.Pin_0
  N3: Onderdeel1.A3, R7.Pin_0, NEXT.Pin_3, NEXT.Pin_4
  N4: Onderdeel1.A4/SDA, INC.Pin_3, INC.Pin_4, R12.Pin_0
  N5: Onderdeel1.A5/SCL, DEC.Pin_3, DEC.Pin_4, R13.Pin_0
  N6: Onderdeel1.D8, Sonar_A.Trig
  N7: Onderdeel1.D9_PWM, Sonar_A.Echo
  N8: Onderdeel1.D10_PWM/SS, R11.Pin_0
  N9: Onderdeel1.D11_PWM/MOSI, LCD_screen.E
  N10: Onderdeel1.D12/MISO, LCD_screen.RS
  N11: Onderdeel1.D13/SCK, R10.Pin_1
  N12: Onderdeel1.D1/TX, R8.Pin_0
  N13: Onderdeel1.D2, LCD_screen.DB7
  N14: Onderdeel1.D3_PWM, LCD_screen.DB6
  N15: Onderdeel1.D4, LCD_screen.DB5
  N16: Onderdeel1.D5_PWM, LCD_screen.DB4
  N17: Onderdeel1.D6_PWM, Sonar_B.Trig
  N18: Onderdeel1.D7, Sonar_B.Echo
  VCC: Onderdeel1.5V, LCD_screen.VDD, MODE.Pin_1, MODE.Pin_2, R4.leg1, R3.Pin_0, Sonar_B.VCC, Sonar_A.VCC, R9.Pin_1, NEXT.Pin_1, NEXT.Pin_2, INC.Pin_1, INC.Pin_2, DEC.Pin_1, DEC.Pin_2
  GND: Onderdeel1.GND, LCD_screen.VSS, LCD_screen.R/W, LCD_screen.LED-, R4.leg2, Sonar_B.GND, Sonar_A.GND, MIDI_Out.2, R5.Pin_1, R6.Pin_1, R7.Pin_1, Led_A.cathode, Led_B.cathode, R12.Pin_1, R13.Pin_1
  N19: LCD_screen.V0, R4.wiper
  N20: LCD_screen.LED+, R3.Pin_1
  N21: PREV.Pin_1, PREV.Pin_2
  N22: MIDI_Out.5, R8.Pin_1
  N23: MIDI_Out.4, R9.Pin_0
  N24: Led_A.anode, R11.Pin_1
  N25: Led_B.anode, R10.Pin_0

notes:
  Contrast
  Activity A
  Activity B
  Trigger B
  Echo B
  Trigger A
  Echo A
  LCD Clock
  LCD Reg Select
  LCD Data
  MIDI Out Serial
  10kΩ
  220Ω
